# Fritzing sketch skema (saved by Fritzing 0.8.7b)

parts:
  U1 = ESP8266 NodeMCU LoLin module
  LCM1602_IIC2 = LCM1602 IIC [part_number="LCM1602 IIC" chip_label="LCM1602 IIC" package="DIP (Dual Inline) [THT]"]
  U2 = LCD-16X2 [package=lcd-16x2]
  U3 = SWITCH_SPDT [package=kps-1290]
  C2 = Electrolytic Capacitor [capacitance=100µF package="200 mil [THT, electrolytic]"]
  J1 = Infrared Proximity Sensor
  VCC1 = Battery block 9V
  Part1 = Adafruit PCF8591 [part_number="Adafruit #4648"]
  Part3 = SRF05 Ultrasonic Rangefinder
  CONN1 = USB connector [package=THT]  # not connected
  U4 = Voltage Regulator [package=v-reg_dpack]

nets:
  N1: U1.D1, LCM1602_IIC2.SCL
  N2: U1.D2, LCM1602_IIC2.SDA
  N3: U1.D5, Part3.Echo
  N4: U1.D6, Part3.Trig
  VSS: LCM1602_IIC2.VSS, U2.VSS
  N5: LCM1602_IIC2.V0, U2.VO
  N6: LCM1602_IIC2.RS, U2.RS
  N7: LCM1602_IIC2.RW, U2.R_W
  N8: LCM1602_IIC2.E, U2.E
  N9: LCM1602_IIC2.D0, U2.DB0
  N10: LCM1602_IIC2.D1, U2.DB1
  N11: LCM1602_IIC2.D2, U2.DB2
  N12: LCM1602_IIC2.D3, U2.DB3
  N13: LCM1602_IIC2.D4, U2.DB4
  N14: LCM1602_IIC2.D5, U2.DB5
  N15: LCM1602_IIC2.D6, U2.DB6
  N16: LCM1602_IIC2.D7, U2.DB7
  N17: LCM1602_IIC2.A, U2.A
  N18: LCM1602_IIC2.K, U2.K
  N19: LCM1602_IIC2.VCC, U4.OUT
  N20: LCM1602_IIC2.LED_A, LCM1602_IIC2.LED_B
  N21: U3.O, VCC1.+
  N22: U3.P, U4.ADJ
  N23: C2.-, J1.GND
  N24: J1.Vout, Part1.AIN0
  N25: VCC1.-, U4.IN

notes:
  Elco 10uF
  Saklar
  Regulator LM2596
  Battery 9v
  PCF8591
  LCD 16x2
  LCD to I2C Adapter
  NodeMCU ESP8266
  SHARP GP2Y0A710K0F
  USB
  Ultrasonic HC-SR04

custom parts:
  ESP8266 NodeMCU LoLin module: ESP8266 based NodeMCU
  LCM1602 IIC: I2C-Module to use a 1602 or 2004 LCD on with the wire.h libory Serial LCD Modul
  Adafruit PCF8591: Measuring voltage and adjusting it is what electronics is all about so you won’t get far without friends like the PCF8591 ADC+DAC combo. Analog to Digital Converters help by measuring an analog voltage and turning it into something a microcontroller like a Metro or Arduino can understand. If you’re using a single board computer like a Raspberry Pi, you might not have any other way to measure a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
